// Logisim project lab7.circ as structural Verilog: 3 circuits, main circuit MyXOR
module MyXOR (
  input  X,
  input  X_2,
  output Z
);

  wire and_1_out, and_2_out, not_1_out, not_2_out;

  not not_1 (not_1_out, X);
  not not_2 (not_2_out, X_2);
  and and_1 (and_1_out, not_1_out, X_2);
  and and_2 (and_2_out, X, not_2_out, not_2_out);
  or or_1 (Z, and_1_out, and_2_out);

  // Notes on the sheet:
  //   Here is a location to build an XOR circuit
  //   We already implemented this circuit in class.  Copy it here.
endmodule

module FullAdder (
  input  X,
  input  Y,
  input  CarryIn,
  output sum,
  output CarryOut
);

  wire and_1_out, and_2_out, and_3_out, and_4_out, and_5_out, and_6_out, not_1_out, not_2_out, not_3_out,
       not_4_out, or_1_out;

  not not_1 (not_1_out, X);
  not not_2 (not_2_out, Y);
  and and_1 (and_1_out, not_1_out, not_1_out, Y);
  and and_2 (and_2_out, X, not_2_out);
  and and_3 (and_3_out, or_1_out, CarryIn);
  and and_4 (and_4_out, Y, X);
  or or_1 (or_1_out, and_1_out, and_2_out);
  or or_2 (CarryOut, and_3_out, and_4_out);
  not not_3 (not_3_out, CarryIn);
  not not_4 (not_4_out, or_1_out);
  and and_5 (and_5_out, not_3_out, or_1_out);
  and and_6 (and_6_out, CarryIn, not_4_out);
  or or_3 (sum, and_5_out, and_6_out);
endmodule

module _4_bit_Ripple_Carry_Adder (
  input  Y3,
  input  Y2,
  input  Y1,
  input  Y0,
  input  X3,
  input  X2,
  input  X1,
  input  X0,
  output Sum4,
  output Sum3,
  output Sum2,
  output Sum1,
  output Sum0
);

  wire fulladder_2_carryout, fulladder_3_carryout, fulladder_4_carryout;

  FullAdder fulladder_1 (.X(Y3), .Y(X3), .CarryIn(fulladder_2_carryout), .sum(Sum3), .CarryOut(Sum4));
  FullAdder fulladder_2 (.X(Y2), .Y(X2), .CarryIn(fulladder_3_carryout), .sum(Sum2), .CarryOut(fulladder_2_carryout));
  FullAdder fulladder_3 (.X(Y1), .Y(X1), .CarryIn(fulladder_4_carryout), .sum(Sum1), .CarryOut(fulladder_3_carryout));
  FullAdder fulladder_4 (.X(Y0), .Y(X0), .CarryIn(1'b0), .sum(Sum0), .CarryOut(fulladder_4_carryout));
endmodule
